# Fritzing sketch Pet_Necklace_ATTiny85 (saved by Fritzing 0.9.3b)
breadboards: 3

parts:
  LED1 = LED - 5mm [color="Green (565nm)" package="5 mm [THT]"]  # not connected
  LED2 = LED - 5mm [color="Blue (525nm)" package="5 mm [THT]"]
  R2 = Resistor [tolerance=±5% resistance=75 package=THT]
  S2 = Tilt Switch [package=THT]
  U1 = attiny85 [package=dip]
  R3 = Photocell (LDR) [package=THT]
  R4 = Resistor [tolerance=±5% resistance=75 package=THT]
  R5 = Resistor [tolerance=±5% resistance=4.7k package=THT]
  LED3 = LED - 5mm [color="Blue (525nm)" package="5 mm [THT]"]
  LED4 = LED - 5mm [color="Blue (525nm)" package="5 mm [THT]"]
  LED5 = LED - 5mm [color="Blue (525nm)" package="5 mm [THT]"]
  LED6 = LED - 5mm [color="Blue (525nm)" package="5 mm [THT]"]
  LED7 = LED - 5mm [color="Blue (525nm)" package="5 mm [THT]"]
  R6 = Resistor [tolerance=±5% resistance=75 package=THT]
  R7 = Resistor [tolerance=±5% resistance=75 package=THT]
  R8 = Resistor [tolerance=±5% resistance=75 package=THT]
  R9 = Resistor [tolerance=±5% resistance=75 package=THT]
  R10 = Resistor [tolerance=±5% resistance=75 package=THT]
  BAT1 = Battery Holders [package=battcom_20mm_pth]

nets:
  N1: LED2.cathode, R4.Pin_0
  N2: LED2.anode, U1.Pin_5, LED4.anode, LED6.anode
  N3: R2.Pin_0, R2.Pin_1, U1.Pin_4, R3.pin_1, BAT1.+
  N4: S2.Pin_1, U1.Pin_8, R4.Pin_1, R5.Pin_0, R6.Pin_1, R7.Pin_1, R8.Pin_1, R9.Pin_1, R10.Pin_1, BAT1.-
  N5: S2.Pin_2, U1.Pin_2
  N6: U1.Pin_6, LED3.anode, LED5.anode, LED7.anode
  N7: U1.Pin_7, R3.pin_0, R5.Pin_1
  N8: LED3.cathode, R6.Pin_0
  N9: LED4.cathode, R7.Pin_0
  N10: LED5.cathode, R8.Pin_0
  N11: LED6.cathode, R9.Pin_0
  N12: LED7.cathode, R10.Pin_0

notes:
  PHOTOCELL
  TILT SWITCH
  PB3
  Necklace LEDs
  Pendant LED
  PB1
  PB0
  ATTiny85
  PB4
  PB2
  DETACHED FOR EASY ACCESS
  CR2032
